// Logisim project algebool-finaldigito.circ as structural Verilog: 4 circuits, main circuit main
module main (
  input  A1,
  input  B1,
  input  C1,
  input  D1,
  input  E1,
  input  A2,
  input  B2,
  input  C2,
  input  D2,
  input  E2,
  output Overflow,
  output A,
  output B,
  output C,
  output D,
  output E
);

  wire digito_1_1_f0, digito_1_1_f1, digito_1_1_f2, digito_1_1_f3, digito_1_1_f4, digito_1_1_f5,
       digito_1_1_f6, digito_2_1_f0, digito_2_1_f1, digito_2_1_f2, digito_2_1_f3, digito_2_1_f4,
       digito_2_1_f5, digito_2_1_f6, digito_3_1_f0, digito_3_1_f1, digito_3_1_f2, digito_3_1_f3,
       digito_3_1_f4, digito_3_1_f5, digito_3_1_f6;

  Soma soma_1 (
    .A1(A1), .B1(B1), .C1(C1), .D1(D1), .E1(E1), .A2(A2), .B2(B2), .C2(C2), .D2(D2), .E2(E2), .A(A), .B(B),
    .C(C), .D(D), .E(E), .Overflow(Overflow));  // open: Enable
  Digito_3 digito_3_1 (
    .A(A), .B(B), .C(C), .D(D), .E(E), .F0(digito_3_1_f0), .F1(digito_3_1_f1), .F2(digito_3_1_f2),
    .F3(digito_3_1_f3), .F4(digito_3_1_f4), .F5(digito_3_1_f5), .F6(digito_3_1_f6));
  Digito_1 digito_1_1 (
    .A(A), .B(B), .C(C), .D(D), .E(E), .F0(digito_1_1_f0), .F1(digito_1_1_f1), .F2(digito_1_1_f2),
    .F3(digito_1_1_f3), .F4(digito_1_1_f4), .F5(digito_1_1_f5), .F6(digito_1_1_f6));
  Digito_2 digito_2_1 (
    .A(A), .B(B), .C(C), .D(D), .E(E), .F0(digito_2_1_f0), .F1(digito_2_1_f1), .F5(digito_2_1_f5),
    .F6(digito_2_1_f6), .F4(digito_2_1_f4), .F2(digito_2_1_f2), .F3(digito_2_1_f3));
  _7_Segment_Display #(.active("true")) u_7_segment_display_1 (
    .g(digito_1_1_f6), .f(digito_1_1_f5), .a(digito_1_1_f0), .b(digito_1_1_f1), .e(digito_1_1_f4),
    .d(digito_1_1_f3), .c(digito_1_1_f2));  // open: dp
  _7_Segment_Display #(.active("true")) u_7_segment_display_2 (
    .g(digito_3_1_f6), .f(digito_3_1_f5), .a(digito_3_1_f0), .b(digito_3_1_f1), .e(digito_3_1_f4),
    .d(digito_3_1_f3), .c(digito_3_1_f2));  // open: dp
  _7_Segment_Display #(.active("true")) u_7_segment_display_3 (
    .g(digito_2_1_f6), .f(digito_2_1_f5), .a(digito_2_1_f0), .b(digito_2_1_f1), .e(digito_2_1_f4),
    .d(digito_2_1_f3), .c(digito_2_1_f2));  // open: dp
endmodule

module Digito_1 (
  input  A,
  input  B,
  input  C,
  input  D,
  input  E,
  output F3,
  output F0,
  output F1,
  output F4,
  output F5,
  output F2,
  output F6
);

  wire and_1_out, and_2_out, and_3_out, not_1_out, not_2_out, not_3_out, not_4_out;

  not not_1 (not_1_out, B);
  not not_2 (not_2_out, C);
  not not_3 (not_3_out, D);
  not not_4 (not_4_out, E);
  and and_1 (and_1_out, A, not_1_out, not_2_out);
  and and_2 (and_2_out, A, not_1_out, not_3_out);
  and and_3 (and_3_out, A, not_1_out, not_4_out);
  or or_1 (F6, and_1_out, and_2_out, and_3_out);

  assign F0 = 1'b0;
  assign F1 = 1'b0;
  assign F2 = 1'b0;
  assign F3 = 1'b0;
  assign F4 = 1'b0;
  assign F5 = 1'b0;
endmodule

module Digito_2 (
  input  A,
  input  B,
  input  C,
  input  D,
  input  E,
  output F0,
  output F4,
  output F5,
  output F3,
  output F1,
  output F2,
  output F6
);

  wire and_1_out, and_2_out, and_3_out, and_4_out, and_5_out, and_6_out, and_7_out, not_1_out, not_2_out,
       not_3_out, not_4_out, not_5_out;

  not not_1 (not_1_out, A);
  not not_2 (not_2_out, B);
  not not_3 (not_3_out, C);
  not not_4 (not_4_out, D);
  not not_5 (not_5_out, E);
  and and_1 (and_1_out, B, A);
  and and_2 (and_2_out, E, D, C, A);
  or or_1 (F6, and_1_out, and_2_out);
  and and_3 (and_3_out, not_1_out, B, C);
  and and_4 (and_4_out, not_1_out, B, D);
  and and_5 (and_5_out, A, not_2_out, not_4_out);
  and and_6 (and_6_out, A, not_2_out, not_3_out);
  and and_7 (and_7_out, not_5_out, A, not_2_out);
  or or_2 (F1, and_3_out, and_4_out, and_5_out, and_6_out, and_7_out);

  assign F0 = 1'b0;
  assign F2 = F1;
  assign F3 = 1'b0;
  assign F4 = 1'b0;
  assign F5 = 1'b0;
endmodule

module Digito_3 (
  input  A,
  input  B,
  input  C,
  input  D,
  input  E,
  output F0,
  output F1,
  output F2,
  output F3,
  output F4,
  output F5,
  output F6
);

  wire and_1_out, and_2_out, and_3_out, and_4_out, and_5_out, and_6_out, and_7_out, and_8_out, and_9_out,
       and_10_out, and_11_out, and_12_out, and_13_out, and_14_out, and_15_out, and_16_out, and_17_out,
       and_18_out, and_19_out, and_20_out, and_21_out, and_22_out, and_23_out, not_1_out, not_2_out,
       not_3_out, not_4_out, not_5_out, or_1_out, or_2_out, or_3_out, or_7_out, or_10_out, or_12_out,
       or_13_out;

  not not_1 (not_1_out, A);
  and and_1 (and_1_out, A, B, not_3_out, D);
  not not_2 (not_2_out, B);
  and and_2 (and_2_out, A, B, D, not_5_out);
  or or_1 (or_1_out, and_1_out, and_2_out, and_3_out, and_4_out, and_5_out, and_6_out, and_7_out, and_8_out, and_9_out);
  not not_3 (not_3_out, C);
  and and_3 (and_3_out, A, not_2_out, not_3_out, not_4_out);
  or or_2 (or_2_out, and_10_out, and_12_out, and_14_out);
  or or_3 (or_3_out, and_11_out, and_13_out);
  or or_4 (F0, or_1_out, or_3_out, or_2_out);
  not not_4 (not_4_out, D);
  not not_5 (not_5_out, E);
  and and_4 (and_4_out, A, not_2_out, not_4_out, not_5_out);
  or or_5 (F1, and_6_out, and_11_out, and_13_out, and_16_out, and_15_out, and_17_out, and_18_out, and_19_out, and_9_out);
  and and_5 (and_5_out, not_1_out, B, C, D, E);
  and and_6 (and_6_out, not_1_out, B, not_4_out, not_5_out);
  or or_6 (F2, and_10_out, and_12_out, and_14_out, and_16_out, and_17_out, and_18_out, E, and_20_out);
  and and_7 (and_7_out, not_1_out, not_2_out, C, not_4_out, E);
  and and_8 (and_8_out, not_1_out, not_2_out, D, not_5_out);
  or or_7 (or_7_out, and_21_out, and_22_out, and_23_out);
  or or_8 (F3, or_1_out, or_7_out, or_2_out);
  and and_9 (and_9_out, B, C, not_4_out, E);
  or or_9 (F4, and_2_out, and_4_out, and_6_out, and_10_out, and_8_out, and_12_out, and_14_out);
  and and_10 (and_10_out, B, not_3_out, not_5_out);
  and and_11 (and_11_out, B, not_3_out, not_4_out);
  or or_10 (or_10_out, and_1_out, and_3_out, and_5_out, and_7_out, and_10_out, and_12_out, and_14_out, and_16_out, and_17_out);
  or or_11 (F5, or_10_out, or_12_out);
  and and_12 (and_12_out, not_2_out, C, D, not_5_out);
  or or_12 (or_12_out, and_18_out, and_20_out, and_21_out, and_22_out);
  and and_13 (and_13_out, not_2_out, D, E);
  or or_13 (or_13_out, and_16_out, and_17_out, and_18_out, and_20_out, and_21_out, and_22_out, and_23_out);
  or or_14 (F6, or_1_out, or_13_out);
  and and_14 (and_14_out, not_3_out, not_4_out, not_5_out);
  and and_15 (and_15_out, A, C);
  and and_16 (and_16_out, A, not_2_out, not_3_out, D, not_5_out);
  and and_17 (and_17_out, not_1_out, B, C, D, not_5_out);
  and and_18 (and_18_out, not_1_out, not_2_out, C, not_4_out, not_5_out);
  and and_19 (and_19_out, not_1_out, not_3_out);
  and and_20 (and_20_out, A, B, not_4_out, not_5_out);
  and and_21 (and_21_out, A, not_2_out, C, D, E);
  and and_22 (and_22_out, not_1_out, B, not_3_out, not_4_out);
  and and_23 (and_23_out, not_2_out, not_3_out, D, E);

  // Notes on the sheet:
  //   A B C'D   
  //   1
  //   A B   D E'
  //   2
  //   A B'C'D'  
  //   3
  //   AB'D'E'
  //   4
  //   A'BCDE
  //   5
  //   6
  //   A'B'CD'E
  //   A'BD'E'
  //   7
  //   A'B'DE'
  //   8
  //   BCD'E
  //   9
  //   BC'E'
  //   10
  //   B C'D'
  //   11
  //   B'CDE'
  //   12
  //   B'DE
  //   13
  //   14
  //   C'D'E'
  //   15
  //   AB'C'DE'
  //   AC
  //   16
  //   A'BCDE'
  //   17
  //   A'B'CD'E'
  //   18
  //   A'C'
  //   19
  //   ABD'E'
  //   21
  //   20
  //   AB'CDE
  //   22
  //   A'BC'D'
  //   B'C'DE
  //   23
endmodule
