// Logisim project display5bit.circ as structural Verilog: 3 circuits, main circuit main
module main (
  input  in_1,
  input  in_2,
  input  in_3,
  input  in_4,
  input  in_5
);

  wire digito_3_1_f0, digito_3_1_f1, digito_3_1_f2, digito_3_1_f3, digito_3_1_f4, digito_3_1_f5,
       digito_3_1_f6, modulo_1_ma, modulo_1_mb, modulo_1_mc, modulo_1_md, modulo_1_me;

  Digito_3 digito_3_1 (
    .a(modulo_1_ma), .b(modulo_1_mb), .c(modulo_1_mc), .d(modulo_1_md), .e(modulo_1_me), .f0(digito_3_1_f0),
    .f1(digito_3_1_f1), .f2(digito_3_1_f2), .f3(digito_3_1_f3), .f4(digito_3_1_f4), .f5(digito_3_1_f5),
    .f6(digito_3_1_f6));
  Modulo modulo_1 (
    .a(in_1), .b(in_2), .c(in_3), .d(in_4), .e(in_5), .mA(modulo_1_ma), .mB(modulo_1_mb), .mC(modulo_1_mc),
    .mD(modulo_1_md), .mE(modulo_1_me));
  _7_Segment_Display #(.active("true")) u_7_segment_display_1 ();  // open: g, f, a, b, e, d, c, dp
  _7_Segment_Display #(.active("true")) u_7_segment_display_2 ();  // open: g, f, a, b, e, d, c, dp
  _7_Segment_Display #(.active("false")) u_7_segment_display_3 (
    .g(digito_3_1_f6), .f(digito_3_1_f5), .a(digito_3_1_f0), .b(digito_3_1_f1), .e(digito_3_1_f4),
    .d(digito_3_1_f3), .c(digito_3_1_f2), .dp(1'b1));
endmodule

module Digito_3 (
  input  a,
  input  b,
  input  c,
  input  d,
  input  e,
  output f0,
  output f1,
  output f2,
  output f3,
  output f4,
  output f5,
  output f6
);

  wire and_1_out, and_2_out, and_3_out, and_4_out, and_5_out, and_6_out, and_7_out, and_8_out, and_9_out,
       and_10_out, and_11_out, and_12_out, and_13_out, and_14_out, and_15_out, and_16_out, and_17_out,
       and_18_out, and_19_out, and_20_out, and_21_out, and_22_out, and_23_out, and_24_out, not_1_out,
       not_2_out, not_3_out, not_4_out, not_5_out, not_6_out, not_7_out, not_8_out, not_9_out, not_10_out,
       not_11_out, not_12_out, not_13_out, not_14_out, not_15_out, not_16_out, not_17_out, not_18_out,
       not_19_out, not_20_out, not_21_out, not_22_out, not_23_out, not_24_out, not_25_out, not_26_out,
       not_27_out, not_28_out, not_29_out, not_30_out, not_31_out, not_32_out, not_33_out, not_34_out,
       not_35_out, not_36_out, not_37_out, not_38_out, not_39_out, not_40_out, not_41_out;

  not not_1 (not_1_out, b);
  not not_2 (not_2_out, c);
  not not_3 (not_3_out, d);
  not not_4 (not_4_out, b);
  not not_5 (not_5_out, d);
  not not_6 (not_6_out, e);
  not not_7 (not_7_out, c);
  not not_8 (not_8_out, e);
  not not_9 (not_9_out, b);
  not not_10 (not_10_out, d);
  not not_11 (not_11_out, b);
  not not_12 (not_12_out, e);
  not not_13 (not_13_out, b);
  not not_14 (not_14_out, c);
  not not_15 (not_15_out, e);
  not not_16 (not_16_out, d);
  not not_17 (not_17_out, e);
  not not_18 (not_18_out, b);
  not not_19 (not_19_out, c);
  not not_20 (not_20_out, d);
  not not_21 (not_21_out, b);
  not not_22 (not_22_out, d);
  not not_23 (not_23_out, e);
  not not_24 (not_24_out, b);
  not not_25 (not_25_out, c);
  not not_26 (not_26_out, e);
  not not_27 (not_27_out, b);
  not not_28 (not_28_out, d);
  not not_29 (not_29_out, b);
  not not_30 (not_30_out, c);
  not not_31 (not_31_out, b);
  not not_32 (not_32_out, c);
  not not_33 (not_33_out, b);
  not not_34 (not_34_out, c);
  not not_35 (not_35_out, d);
  not not_36 (not_36_out, a);
  not not_37 (not_37_out, b);
  not not_38 (not_38_out, c);
  not not_39 (not_39_out, d);
  not not_40 (not_40_out, b);
  not not_41 (not_41_out, c);
  and and_1 (and_1_out, not_1_out, not_2_out, 1'b1, not_3_out, e);
  and and_2 (and_2_out, not_4_out, c, 1'b1, not_5_out, not_6_out);
  and and_3 (and_3_out, b, not_7_out, 1'b1, d, e);
  and and_4 (and_4_out, b, c, 1'b1, d, not_8_out);
  and and_5 (and_5_out, not_9_out, c, 1'b1, not_10_out, e);
  and and_6 (and_6_out, not_11_out, c, 1'b1, d, not_12_out);
  and and_7 (and_7_out, b, c, 1'b1, d, e);
  and and_8 (and_8_out, not_13_out, not_14_out, 1'b1, d, not_15_out);
  and and_9 (and_9_out, b, c, 1'b1, not_16_out, not_17_out);
  and and_10 (and_10_out, not_18_out, not_19_out, 1'b1, not_20_out, e);
  and and_11 (and_11_out, not_21_out, c, 1'b1, not_22_out, not_23_out);
  and and_12 (and_12_out, not_24_out, c, 1'b1, d, e);
  and and_13 (and_13_out, b, not_25_out, 1'b1, d, e);
  and and_14 (and_14_out, b, c, 1'b1, d, not_26_out);
  and and_15 (and_15_out, not_27_out, c, not_28_out);
  and and_16 (and_16_out, b, c, d);
  and and_17 (and_17_out, not_29_out, not_30_out, e);
  and and_18 (and_18_out, not_31_out, not_32_out, d);
  and and_19 (and_19_out, not_33_out, d, e);
  and and_20 (and_20_out, not_34_out, d, e);
  and and_21 (and_21_out, b, c, not_35_out);
  and and_22 (and_22_out, not_36_out, not_37_out, 1'b1, not_38_out, not_39_out);
  and and_23 (and_23_out, not_40_out, c, 1'b1, d, e);
  and and_24 (and_24_out, b, not_41_out, d);
  or or_1 (f0, and_1_out, and_2_out, 1'b0, and_3_out, and_4_out);
  or or_2 (f1, and_5_out, and_6_out, 1'b0, and_7_out, a);
  or or_3 (f2, and_8_out, and_9_out);
  or or_4 (f3, and_10_out, and_11_out, and_12_out, and_13_out, and_14_out);
  or or_5 (f4, e, and_15_out, and_16_out);
  or or_6 (f5, and_17_out, and_18_out, and_19_out, and_20_out, and_21_out);
  or or_7 (f6, and_22_out, and_23_out, and_24_out);
endmodule

module Modulo (
  input  a,
  input  b,
  input  c,
  input  d,
  input  e,
  output mA,
  output mB,
  output mC,
  output mD,
  output mE
);

  wire and_2_out, and_3_out, and_4_out, and_5_out, and_6_out, and_7_out, and_8_out, and_9_out, and_10_out,
       and_11_out, and_12_out, and_13_out, not_1_out, not_2_out, not_3_out, not_4_out, not_5_out, not_6_out,
       not_7_out, not_8_out, not_9_out, not_10_out, not_11_out, not_12_out, not_13_out, not_14_out,
       not_15_out, not_16_out, not_17_out, not_18_out, not_19_out;

  not not_1 (not_1_out, b);
  not not_2 (not_2_out, c);
  not not_3 (not_3_out, d);
  not not_4 (not_4_out, e);
  not not_5 (not_5_out, a);
  not not_6 (not_6_out, c);
  not not_7 (not_7_out, d);
  not not_8 (not_8_out, e);
  not not_9 (not_9_out, b);
  not not_10 (not_10_out, b);
  not not_11 (not_11_out, b);
  not not_12 (not_12_out, a);
  not not_13 (not_13_out, d);
  not not_14 (not_14_out, e);
  not not_15 (not_15_out, c);
  not not_16 (not_16_out, c);
  not not_17 (not_17_out, a);
  not not_18 (not_18_out, e);
  not not_19 (not_19_out, d);
  and and_1 (mA, a, not_1_out, not_2_out, not_3_out, not_4_out);
  and and_2 (and_2_out, not_5_out, b);
  and and_3 (and_3_out, b, not_6_out, 1'b1, not_7_out, not_8_out);
  and and_4 (and_4_out, a, not_9_out, e);
  and and_5 (and_5_out, a, not_10_out, d);
  and and_6 (and_6_out, a, not_11_out, c);
  and and_7 (and_7_out, not_12_out, c);
  and and_8 (and_8_out, c, not_13_out, not_14_out);
  and and_9 (and_9_out, a, not_15_out, e);
  and and_10 (and_10_out, a, not_16_out, d);
  and and_11 (and_11_out, not_17_out, d);
  and and_12 (and_12_out, d, not_18_out);
  and and_13 (and_13_out, a, not_19_out, e);
  or or_1 (mB, and_2_out, and_3_out, and_4_out, and_5_out, and_6_out);
  or or_2 (mC, and_7_out, and_8_out, 1'b0, and_9_out, and_10_out);
  or or_3 (mD, and_11_out, and_12_out, and_13_out);

  assign mE = e;
endmodule
