// Logisim project soma.circ as structural Verilog: 2 circuits, main circuit Soma
module Circuito_Soma (
  input  A,
  input  B,
  input  C,
  output Carry,
  output Output
);

  wire and_1_out, and_2_out, and_3_out, and_4_out, and_5_out, and_6_out, and_7_out, not_1_out, not_2_out,
       not_3_out;

  not not_1 (not_1_out, A);
  not not_2 (not_2_out, B);
  not not_3 (not_3_out, C);
  and and_1 (and_1_out, A, B);
  and and_2 (and_2_out, A, C);
  and and_3 (and_3_out, B, C);
  and and_4 (and_4_out, A, B, C);
  and and_5 (and_5_out, not_1_out, not_2_out, C);
  and and_6 (and_6_out, not_1_out, B, not_3_out);
  and and_7 (and_7_out, A, not_2_out, not_3_out);
  or or_1 (Carry, and_1_out, and_2_out, and_3_out);
  or or_2 (Output, and_4_out, and_5_out, and_6_out, and_7_out);
endmodule

module Soma (
  input  A1,
  input  B1,
  input  C1,
  input  D1,
  input  E1,
  input  A2,
  input  B2,
  input  C2,
  input  D2,
  input  E2,
  input  Enable,
  output A,
  output B,
  output C,
  output D,
  output E,
  output Overflow
);

  wire and_1_out, and_2_out, and_3_out, and_4_out, and_5_out, and_6_out, and_7_out, and_8_out, and_9_out,
       and_10_out, circuito_soma_1_carry, circuito_soma_2_carry, circuito_soma_3_carry,
       circuito_soma_4_carry, circuito_soma_5_carry;

  Circuito_Soma circuito_soma_1 (.A(1'b0), .B(and_5_out), .C(and_10_out), .Carry(circuito_soma_1_carry), .Output(E));
  and and_1 (and_1_out, A1, Enable);
  and and_2 (and_2_out, B1, Enable);
  and and_3 (and_3_out, C1, Enable);
  and and_4 (and_4_out, D1, Enable);
  and and_5 (and_5_out, E1, Enable);
  and and_6 (and_6_out, A2, Enable);
  and and_7 (and_7_out, B2, Enable);
  and and_8 (and_8_out, C2, Enable);
  and and_9 (and_9_out, D2, Enable);
  and and_10 (and_10_out, E2, Enable);
  Circuito_Soma circuito_soma_2 (
    .A(circuito_soma_1_carry), .B(and_4_out), .C(and_9_out), .Carry(circuito_soma_2_carry), .Output(D));
  Circuito_Soma circuito_soma_3 (
    .A(circuito_soma_2_carry), .B(and_3_out), .C(and_8_out), .Carry(circuito_soma_3_carry), .Output(C));
  Circuito_Soma circuito_soma_4 (
    .A(circuito_soma_3_carry), .B(and_2_out), .C(and_7_out), .Carry(circuito_soma_4_carry), .Output(B));
  Circuito_Soma circuito_soma_5 (
    .A(circuito_soma_4_carry), .B(and_1_out), .C(and_6_out), .Carry(circuito_soma_5_carry), .Output(A));
  xor xor_1 (Overflow, circuito_soma_5_carry, circuito_soma_4_carry);
endmodule
