// Logisim project yaycircuito.circ as structural Verilog
module main (
  input  E0,
  input  E1,
  input  E2,
  input  E3,
  input  E4,
  input  Input_Finished,
  input  First,
  input  Second,
  output Overflow
);

  wire demux_4_1_f0, demux_4_1_f1, demux_4_1_f2, demux_4_1_f3, digito_1_1_f0, digito_1_1_f1, digito_1_1_f2,
       digito_1_1_f3, digito_1_1_f4, digito_1_1_f5, digito_1_1_f6, digito_2_1_f0, digito_2_1_f1,
       digito_2_1_f2, digito_2_1_f3, digito_2_1_f4, digito_2_1_f5, digito_2_1_f6, digito_3_1_f0,
       digito_3_1_f1, digito_3_1_f2, digito_3_1_f3, digito_3_1_f4, digito_3_1_f5, digito_3_1_f6,
       memoria_5bit_1_out_bit_0, memoria_5bit_1_out_bit_1, memoria_5bit_1_out_bit_2,
       memoria_5bit_1_out_bit_3, memoria_5bit_1_out_bit_4, multiplicacao_1_a, multiplicacao_1_b,
       multiplicacao_1_c, multiplicacao_1_d, multiplicacao_1_e, multiplicacao_1_overflow, soma_1_a, soma_1_b,
       soma_1_c, soma_1_d, soma_1_e, soma_1_overflow, subtracao_1_a, subtracao_1_b, subtracao_1_c,
       subtracao_1_d, subtracao_1_e, subtracao_1_overflow, unir_15_em_5_1_s0, unir_15_em_5_1_s1,
       unir_15_em_5_1_s2, unir_15_em_5_1_s3, unir_15_em_5_1_s4;

  Demux_4 demux_4_1 (
    .I0(Input_Finished), .S1(First), .S0(Second), .F3(demux_4_1_f3), .F2(demux_4_1_f2), .F1(demux_4_1_f1),
    .F0(demux_4_1_f0));
  Memoria_5bit memoria_5bit_1 (
    .Bit_0(E0), .Bit_1(E1), .Bit_2(E2), .Bit_3(E3), .Bit_4(E4), .Clock(demux_4_1_f0),
    .Out_Bit_0(memoria_5bit_1_out_bit_0), .Out_Bit_1(memoria_5bit_1_out_bit_1),
    .Out_Bit_2(memoria_5bit_1_out_bit_2), .Out_Bit_3(memoria_5bit_1_out_bit_3),
    .Out_Bit_4(memoria_5bit_1_out_bit_4));
  Soma soma_1 (
    .A1(memoria_5bit_1_out_bit_0), .B1(memoria_5bit_1_out_bit_1), .C1(memoria_5bit_1_out_bit_2),
    .D1(memoria_5bit_1_out_bit_3), .E1(memoria_5bit_1_out_bit_4), .A2(E0), .B2(E1), .C2(E2), .D2(E3),
    .E2(E4), .Enable(demux_4_1_f1), .A(soma_1_a), .B(soma_1_b), .C(soma_1_c), .D(soma_1_d), .E(soma_1_e),
    .Overflow(soma_1_overflow));
  Subtracao subtracao_1 (
    .A1(memoria_5bit_1_out_bit_0), .B1(memoria_5bit_1_out_bit_1), .C1(memoria_5bit_1_out_bit_2),
    .D1(memoria_5bit_1_out_bit_3), .E1(memoria_5bit_1_out_bit_4), .A2(E0), .B2(E1), .C2(E2), .D2(E3),
    .E2(E4), .Enable(demux_4_1_f2), .A(subtracao_1_a), .B(subtracao_1_b), .C(subtracao_1_c),
    .D(subtracao_1_d), .E(subtracao_1_e), .Overflow(subtracao_1_overflow));
  Multiplicacao multiplicacao_1 (
    .A1(memoria_5bit_1_out_bit_0), .B1(memoria_5bit_1_out_bit_1), .C1(memoria_5bit_1_out_bit_2),
    .D1(memoria_5bit_1_out_bit_3), .E1(memoria_5bit_1_out_bit_4), .A2(E0), .B2(E1), .C2(E2), .D2(E3),
    .E2(E4), .Enable(demux_4_1_f3), .A(multiplicacao_1_a), .B(multiplicacao_1_b), .C(multiplicacao_1_c),
    .D(multiplicacao_1_d), .E(multiplicacao_1_e), .Overflow(multiplicacao_1_overflow));
  Digito_3 digito_3_1 (
    .A(unir_15_em_5_1_s0), .B(unir_15_em_5_1_s1), .C(unir_15_em_5_1_s2), .D(unir_15_em_5_1_s3),
    .E(unir_15_em_5_1_s4), .F0(digito_3_1_f0), .F1(digito_3_1_f1), .F2(digito_3_1_f2), .F3(digito_3_1_f3),
    .F4(digito_3_1_f4), .F5(digito_3_1_f5), .F6(digito_3_1_f6));
  Unir_15_em_5 unir_15_em_5_1 (
    .A0(soma_1_a), .A1(soma_1_b), .A2(soma_1_c), .A3(soma_1_d), .A4(soma_1_e), .A_Overflow(soma_1_overflow),
    .B0(subtracao_1_a), .B1(subtracao_1_b), .B2(subtracao_1_c), .B3(subtracao_1_d), .B4(subtracao_1_e),
    .B_Overflow(subtracao_1_overflow), .C0(multiplicacao_1_a), .C1(multiplicacao_1_b),
    .C2(multiplicacao_1_c), .C3(multiplicacao_1_d), .C4(multiplicacao_1_e),
    .C_Overflow(multiplicacao_1_overflow), .S0(unir_15_em_5_1_s0), .S1(unir_15_em_5_1_s1),
    .S2(unir_15_em_5_1_s2), .S3(unir_15_em_5_1_s3), .S4(unir_15_em_5_1_s4), .Overflow(Overflow));
  Digito_2 digito_2_1 (
    .A(unir_15_em_5_1_s0), .B(unir_15_em_5_1_s1), .C(unir_15_em_5_1_s2), .D(unir_15_em_5_1_s3),
    .E(unir_15_em_5_1_s4), .F0(digito_2_1_f0), .F1(digito_2_1_f1), .F5(digito_2_1_f5), .F6(digito_2_1_f6),
    .F4(digito_2_1_f4), .F2(digito_2_1_f2), .F3(digito_2_1_f3));
  Digito_1 digito_1_1 (
    .A(unir_15_em_5_1_s0), .B(unir_15_em_5_1_s1), .C(unir_15_em_5_1_s2), .D(unir_15_em_5_1_s3),
    .E(unir_15_em_5_1_s4), .F0(digito_1_1_f0), .F1(digito_1_1_f1), .F2(digito_1_1_f2), .F3(digito_1_1_f3),
    .F4(digito_1_1_f4), .F5(digito_1_1_f5), .F6(digito_1_1_f6));
  _7_Segment_Display #(.active("true")) u_7_segment_display_1 (
    .g(digito_1_1_f6), .f(digito_1_1_f5), .a(digito_1_1_f0), .b(digito_1_1_f2), .e(digito_1_1_f4),
    .d(digito_1_1_f3), .c(digito_1_1_f1));  // open: dp
  _7_Segment_Display #(.active("true")) u_7_segment_display_2 (
    .g(digito_2_1_f6), .f(digito_2_1_f5), .a(digito_2_1_f0), .b(digito_2_1_f1), .e(digito_2_1_f4),
    .d(digito_2_1_f3), .c(digito_2_1_f2));  // open: dp
  _7_Segment_Display #(.active("true")) u_7_segment_display_3 (
    .g(digito_3_1_f6), .f(digito_3_1_f5), .a(digito_3_1_f0), .b(digito_3_1_f1), .e(digito_3_1_f4),
    .d(digito_3_1_f3), .c(digito_3_1_f2));  // open: dp

  // Notes on the sheet:
  //   00 copia para MEM
  //   00 copia para MEM
  //   00 copia para MEM
  //   00 copia para MEM
  //   01 para Soma
  //   01 para Soma
  //   01 para Soma
  //   01 para Soma
  //   01 para Soma
  //   01 para Soma
  //   01 para Soma
  //   01 para Soma
  //   10 para Sub
  //   11 para Soma
  //   11 para Soma
endmodule

module Memoria_5bit (
  input  Bit_0,
  input  Bit_1,
  input  Bit_2,
  input  Bit_3,
  input  Bit_4,
  input  Clock,
  output Out_Bit_0,
  output Out_Bit_1,
  output Out_Bit_2,
  output Out_Bit_3,
  output Out_Bit_4
);

  D_Flip_Flop #(.trigger("rising")) d_ff_1 (
    .clk(Clock), .D(Bit_0), .Q(Out_Bit_0), .en(1'b1));  // open: Qn, preset, reset
  D_Flip_Flop #(.trigger("rising")) d_ff_2 (
    .clk(Clock), .D(Bit_1), .Q(Out_Bit_1), .en(1'b1));  // open: Qn, preset, reset
  D_Flip_Flop #(.trigger("rising")) d_ff_3 (
    .clk(Clock), .D(Bit_2), .Q(Out_Bit_2), .en(1'b1));  // open: Qn, preset, reset
  D_Flip_Flop #(.trigger("rising")) d_ff_4 (
    .clk(Clock), .D(Bit_3), .Q(Out_Bit_3), .en(1'b1));  // open: Qn, preset, reset
  D_Flip_Flop #(.trigger("rising")) d_ff_5 (
    .clk(Clock), .D(Bit_4), .Q(Out_Bit_4), .en(1'b1));  // open: Qn, preset, reset
endmodule

module Demux_4 (
  input  I0,
  input  S1,
  input  S0,
  output F3,
  output F2,
  output F1,
  output F0
);

  wire decoder_4_1_d0, decoder_4_1_d1, decoder_4_1_d2, decoder_4_1_d3;

  Decoder_4 decoder_4_1 (
    .A0(S0), .A1(S1), .D0(decoder_4_1_d0), .D1(decoder_4_1_d1), .D2(decoder_4_1_d2), .D3(decoder_4_1_d3));
  and and_1 (F3, I0, decoder_4_1_d3);
  and and_2 (F2, I0, decoder_4_1_d2);
  and and_3 (F1, I0, decoder_4_1_d1);
  and and_4 (F0, I0, decoder_4_1_d0);
endmodule

module Decoder_4 (
  input  A0,
  input  A1,
  output D0,
  output D1,
  output D2,
  output D3
);

  wire not_1_out, not_2_out;

  not not_1 (not_1_out, A0);
  not not_2 (not_2_out, A1);
  and and_1 (D0, not_1_out, not_2_out);
  and and_2 (D1, A0, not_2_out);
  and and_3 (D2, A1, not_1_out);
  and and_4 (D3, A1, A0);
endmodule

module _5_Bit_Demux_4 (
  input  Enable,
  input  A0,
  input  A1,
  input  A2,
  input  A3,
  input  A4,
  input  S1,
  input  S0,
  output OutA_0,
  output OutA_1,
  output OutA_2,
  output OutA_3,
  output OutA_4,
  output OutB_0,
  output OutB_1,
  output OutB_2,
  output OutB_3,
  output OutB_4,
  output OutC_0,
  output OutC_1,
  output OutC_2,
  output OutC_3,
  output OutC_4,
  output OutD_0,
  output OutD_1,
  output OutD_2,
  output OutD_3,
  output OutD_4
);

  wire and_1_out, and_2_out, and_3_out, and_4_out, and_5_out;

  and and_1 (and_1_out, A0, Enable);
  and and_2 (and_2_out, A1, Enable);
  and and_3 (and_3_out, A2, Enable);
  and and_4 (and_4_out, A3, Enable);
  and and_5 (and_5_out, A4, Enable);
  Demux_4 demux_4_1 (.I0(and_1_out), .S1(S1), .S0(S0), .F3(OutD_0), .F2(OutC_0), .F1(OutB_0), .F0(OutA_0));
  Demux_4 demux_4_2 (.I0(and_2_out), .S1(S1), .S0(S0), .F3(OutD_1), .F2(OutC_1), .F1(OutB_1), .F0(OutA_1));
  Demux_4 demux_4_3 (.I0(and_3_out), .S1(S1), .S0(S0), .F3(OutD_2), .F2(OutC_2), .F1(OutB_2), .F0(OutA_2));
  Demux_4 demux_4_4 (.I0(and_4_out), .S1(S1), .S0(S0), .F3(OutD_3), .F2(OutC_3), .F1(OutB_3), .F0(OutA_3));
  Demux_4 demux_4_5 (.I0(and_5_out), .S1(S1), .S0(S0), .F3(OutD_4), .F2(OutC_4), .F1(OutB_4), .F0(OutA_4));
endmodule

module Subtracao (
  input  A1,
  input  B1,
  input  C1,
  input  D1,
  input  E1,
  input  A2,
  input  B2,
  input  C2,
  input  D2,
  input  E2,
  input  Enable,
  output A,
  output B,
  output C,
  output D,
  output E,
  output Overflow
);

  wire negacao_1_a, negacao_1_b, negacao_1_c, negacao_1_d, negacao_1_e;

  Negacao negacao_1 (
    .A1(A2), .B1(B2), .C1(C2), .D1(D2), .E1(E2), .A(negacao_1_a), .B(negacao_1_b), .C(negacao_1_c),
    .D(negacao_1_d), .E(negacao_1_e));
  Soma soma_1 (
    .A1(A1), .B1(B1), .C1(C1), .D1(D1), .E1(E1), .A2(negacao_1_a), .B2(negacao_1_b), .C2(negacao_1_c),
    .D2(negacao_1_d), .E2(negacao_1_e), .Enable(Enable), .A(A), .B(B), .C(C), .D(D), .E(E),
    .Overflow(Overflow));
endmodule

module Negacao (
  input  A1,
  input  B1,
  input  C1,
  input  D1,
  input  E1,
  output A,
  output B,
  output C,
  output D,
  output E
);

  wire not_1_out, not_2_out, not_3_out, not_4_out, not_5_out;

  not not_1 (not_1_out, A1);
  not not_2 (not_2_out, B1);
  not not_3 (not_3_out, C1);
  Soma soma_1 (
    .A1(not_1_out), .B1(not_2_out), .C1(not_3_out), .D1(not_4_out), .E1(not_5_out), .A2(1'b0), .B2(1'b0),
    .C2(1'b0), .D2(1'b0), .E2(1'b1), .Enable(1'b1), .A(A), .B(B), .C(C), .D(D), .E(E));  // open: Overflow
  not not_4 (not_4_out, D1);
  not not_5 (not_5_out, E1);
endmodule

module Multiplicacao (
  input  A1,
  input  B1,
  input  C1,
  input  D1,
  input  E1,
  input  A2,
  input  B2,
  input  C2,
  input  D2,
  input  E2,
  input  Enable,
  output A,
  output B,
  output C,
  output D,
  output E,
  output Overflow
);
endmodule

module Unir_15_em_5 (
  input  A0,
  input  A1,
  input  A2,
  input  A3,
  input  A4,
  input  A_Overflow,
  input  B0,
  input  B1,
  input  B2,
  input  B3,
  input  B4,
  input  B_Overflow,
  input  C0,
  input  C1,
  input  C2,
  input  C3,
  input  C4,
  input  C_Overflow,
  output Overflow,
  output S0,
  output S1,
  output S2,
  output S3,
  output S4
);

  or or_1 (S0, C0, B0, A0);
  or or_2 (S1, C1, B1, A1);
  or or_3 (S2, C2, B2, A2);
  or or_4 (S3, C3, B3, A3);
  or or_5 (S4, C4, B4, A4);
  or or_6 (Overflow, A_Overflow, B_Overflow, C_Overflow);
endmodule
